// Logisim project RiscVComputer.circ as structural Verilog: 14 circuits, main circuit main
module main (
  input  RESET
);

  wire ALUSrc, branch_taken, CLK, IsBranch, IsJAL, IsJALR, MemRead, MemWrite, RegWrite, take_target;
  wire [1:0] ALUOp, ASel, WBSel;
  wire [2:0] funct3, ImmSel;
  wire [3:0] ALUCtrl;
  wire [4:0] rd, rs1, rs2;
  wire [6:0] funct7, opcode;
  wire [31:0] alu_a, alu_b, alu_result, imm, instr, jalr_target, mem_rdata, next_pc, pc, pc_a, pc_plus4,
       pc_target, rs1_data, rs2_data, wb_data;

  Clock clock_1 (.out(CLK));
  Register #(.width(32)) u_PC (.D(next_pc), .en(1'b1), .clk(CLK), .Q(pc), .clr(RESET));
  // Probe on pc
  // Probe on RegWrite
  // Probe on rs1_data
  Adder #(.width(32)) adder_1 (.a(pc), .b(32'h4), .out(pc_plus4));  // open: cin, cout
  ROM #(.addrWidth(8), .dataWidth(32)) rom_1 (.addr(pc[9:2]), .data(instr));
  // Probe on instr
  // Probe on MemWrite
  // Probe on rs2_data
  InstructionDecode instructiondecode_1 (
    .Instruction(instr), .funct7(funct7), .rs2(rs2), .rs1(rs1), .funct3(funct3), .rd(rd), .opcode(opcode));
  MainControl maincontrol_1 (
    .opcode(opcode), .RegWrite(RegWrite), .ALUSrc(ALUSrc), .MemWrite(MemWrite), .MemRead(MemRead),
    .IsBranch(IsBranch), .ALUOp(ALUOp), .ImmSel(ImmSel), .ASel(ASel), .WBSel(WBSel), .IsJAL(IsJAL),
    .IsJALR(IsJALR));
  ImmGen immgen_1 (.Instruction(instr), .ImmSel(ImmSel), .Imm(imm));
  RegisterFile registerfile_1 (
    .write_data(wb_data), .CLK(CLK), .write(RegWrite), .rd(rd), .rs1(rs1), .rs2(rs2), .rs1_data(rs1_data),
    .rs2_data(rs2_data));
  // Probe on alu_result
  // Probe on ALUSrc
  // Probe on imm
  Multiplexer #(.select(2), .width(32)) multiplexer_1 (
    .in0(rs1_data), .in1(pc), .in2({32{1'b0}}), .in3({32{1'b0}}), .out(alu_a), .sel(ASel));
  Multiplexer #(.select(1), .width(32)) multiplexer_2 (.in0(rs2_data), .in1(imm), .out(alu_b), .sel(ALUSrc));
  Adder #(.width(32)) adder_2 (.a(pc), .b(imm), .out(pc_target));  // open: cin, cout
  assign jalr_target = alu_result & 32'hfffffffe;  // AND_Gate and_1, 32 bits wide
  or or_1 (take_target, branch_taken, IsJAL);
  // Probe on branch_taken
  // Probe on ALUCtrl
  // Probe on mem_rdata
  ALUControl alucontrol_1 (.funct7(funct7), .ALUOp(ALUOp), .funct3(funct3), .ALUCtrl(ALUCtrl));
  ALU alu_1 (.rs1_data(alu_a), .rs2_data(alu_b), .ALU_Ctrl(ALUCtrl), .result(alu_result));
  BranchUnit branchunit_1 (
    .rs1_data(rs1_data), .rs2_data(rs2_data), .IsBranch(IsBranch), .funct3(funct3),
    .branch_taken(branch_taken));
  Multiplexer #(.select(1), .width(32)) multiplexer_3 (.in0(pc_plus4), .in1(pc_target), .out(pc_a), .sel(take_target));
  Multiplexer #(.select(1), .width(32)) multiplexer_4 (.in0(pc_a), .in1(jalr_target), .out(next_pc), .sel(IsJALR));
  // Probe on wb_data
  // Probe on WBSel
  // Probe on next_pc
  Memory memory_1 (
    .Address(alu_result), .write_data(rs2_data), .MemWrite(MemWrite), .CLK(CLK), .funct3(funct3),
    .read_data(mem_rdata));
  Multiplexer #(.select(2), .width(32)) multiplexer_5 (
    .in0(alu_result), .in1(mem_rdata), .in2(pc_plus4), .in3({32{1'b0}}), .out(wb_data), .sel(WBSel));

  // Other names for the same wires on the sheet: pc_word[7:0] = pc[9:2]

  // Notes on the sheet:
  //   Clock: Ctrl+F9 = 1 full cycle
  //   RESET = 1 holds PC at 0
  //   PC register
  //   BẢNG THEO DÕI (probe): xem các giá trị này sau mỗi lần bấm Ctrl+F9
  //   PROBE ĐIỀU KHIỂN (MainControl): lệnh đang chạy bật những tín hiệu nào
  //   PROBE DỮ LIỆU: các giá trị chạy trong datapath
  //   CPU SINGLE-CYCLE (main) - mỗi lệnh chạy trọn vẹn trong MỘT chu kỳ xung nhịp
  //   Vì sao có mạch này: là CPU đơn giản nhất để hiểu; mạch pipeline dùng lại cùng các khối.
  //   IF - Instruction Fetch
  //   PC: địa chỉ lệnh đang được nạp
  //   (tăng 4 mỗi chu kỳ, nhảy khi rẽ nhánh)
  //   vào thanh ghi rd
  //   RegWrite = 1: lệnh sẽ ghi
  //   đọc từ register file
  //   rs1_data: giá trị thanh ghi rs1
  //   PC kế tiếp: lệnh thường -> PC + 4. branch được rẽ hoặc jal -> PC + hằng số (PC + imm). jalr -> (rs1 + imm) với bit 0 bị xóa (AND 0xFFFFFFFE).
  //   BẢNG VIẾT TẮT: PC = Program Counter (bộ đếm chương trình: địa chỉ lệnh đang chạy). ROM = Read Only Memory (bộ nhớ lệnh chỉ đọc). RAM = bộ nhớ dữ liệu đọc/ghi.
  //   PC[9:2] = word address
  //   PC + 4
  //   contents of rom_1 (hex, n*v repeats v):
  //   00000513 00a00593 00b50533 fff58593 fe059ce3 00a02023 00002603 010000ef 40a606b3 0646a713 0000006f
  //   00c60633 00008067 00000000 00000000 00000000
  //   RISC-V RV32I = tập lệnh cơ sở 32 bit số nguyên. imm = hằng số trong lệnh. rd/rs1/rs2 = thanh ghi đích/nguồn 1/nguồn 2. funct3/funct7 = trường chọn biến thể lệnh. NOP = không làm gì.
  //   RESET = 1 giữ PC ở 0. Ctrl+F9 = một chu kỳ = một lệnh. Các probe ở trên cho thấy lệnh sắp chạy và kết quả của nó; tab State cho thấy giá trị thanh ghi sau khi lệnh xong.
  //   Instruction ROM 256 x 32
  //   IF = Instruction Fetch (nạp lệnh). ID = Instruction Decode (giải mã, đọc thanh ghi). EX = Execute (thực thi ở ALU). MEM = Memory access (truy cập RAM). WB = Write Back (ghi kết quả vào thanh ghi).
  //   Các trường hợp theo lệnh: R (add...) ghi ALU vào rd. I (addi...) dùng imm. load: ALU tính địa chỉ, ghi dữ liệu RAM vào rd. store: ghi rs2 vào RAM. branch: so rs1, rs2. lui/auipc/jal/jalr dùng ASel và WBSel.
  //   instr: mã máy 32-bit của lệnh
  //   đang thực thi (đọc từ ROM)
  //   ghi vào RAM dữ liệu
  //   MemWrite = 1: lệnh store,
  //   (cũng là dữ liệu của lệnh store)
  //   rs2_data: giá trị thanh ghi rs2
  //   RV32I single-cycle CPU - top level
  //   One instruction per clock cycle.  Data flows left to right: IF > ID > EX > MEM > WB.  Tunnels with the same name are the same wire.
  //   ID - Decode / Register Read
  //   InstructionDecode
  //   MainControl
  //   ImmGen
  //   RegisterFile
  //   alu_result: kết quả ALU
  //   (số học, địa chỉ load/store)
  //   1 = là hằng số imm
  //   ALUSrc: 0 = toán hạng B là rs2,
  //   mở rộng dấu (ImmGen)
  //   imm: hằng số tức thời đã
  //   Next PC
  //   ALU operand A: 00 rs1   01 PC (auipc)   10 zero (lui)
  //   ALU operand B: 0 rs2   1 imm
  //   PC + imm (branch / JAL target)
  //   JALR target = (rs1 + imm) with bit 0 cleared
  //   EX - Execute and next PC
  //   branch_taken: 1 = lệnh rẽ nhánh
  //   được rẽ, PC nhảy tới đích
  //   2 AND, 3 OR, 4 XOR, 5 SLL, 6 SRL, 7 SRA...)
  //   ALUCtrl: mã phép ALU (0 ADD, 1 SUB,
  //   (chỉ có nghĩa với lệnh load)
  //   mem_rdata: dữ liệu đọc từ RAM
  //   ALUControl
  //   ALU
  //   BranchUnit (beq bne blt bge bltu bgeu)
  //   take_target = branch taken OR JAL
  //   IsJALR selects the register jump
  //   wb_data: giá trị ghi vào thanh ghi rd
  //   ở cuối chu kỳ (write-back)
  //   10 PC+4 (JAL/JALR)
  //   WBSel: 00 ALU, 01 bộ nhớ,
  //   (PC+4, đích rẽ nhánh hoặc JALR)
  //   next_pc: địa chỉ lệnh kế tiếp
  //   MEM - Data Memory
  //   Memory (lb lh lw lbu lhu sb sh sw)
  //   WBSel: 00 ALU   01 memory   10 PC+4 (JAL/JALR)
  //   WB - Write Back
endmodule

module ALU (
  input  [31:0] rs1_data,
  input  [31:0] rs2_data,
  input  [3:0] ALU_Ctrl,
  output [31:0] result
);

  wire comparator_1_lt, comparator_2_lt;
  wire [31:0] adder_1_out, and_1_out, bit_extender_1_out, bit_extender_2_out, or_1_out, shifter_1_out,
       shifter_2_out, shifter_3_out, subtractor_1_out, xor_1_out;

  Adder #(.width(32)) adder_1 (.a(rs1_data), .b(rs2_data), .out(adder_1_out));  // open: cin, cout
  Subtractor #(.width(32)) subtractor_1 (.a(rs1_data), .b(rs2_data), .out(subtractor_1_out));  // open: bin, bout
  Shifter #(.width(32)) shifter_1 (.in(rs1_data), .\dist (rs2_data[4:0]), .out(shifter_1_out));
  Shifter #(.shift("lr"), .width(32)) shifter_2 (.in(rs1_data), .\dist (rs2_data[4:0]), .out(shifter_2_out));
  Shifter #(.shift("ar"), .width(32)) shifter_3 (.in(rs1_data), .\dist (rs2_data[4:0]), .out(shifter_3_out));
  Comparator #(.width(32)) comparator_1 (.a(rs1_data), .b(rs2_data), .lt(comparator_1_lt));  // open: gt, eq
  Comparator #(.mode("unsigned"), .width(32)) comparator_2 (
    .a(rs1_data), .b(rs2_data), .lt(comparator_2_lt));  // open: gt, eq
  assign and_1_out = rs1_data & rs2_data;  // AND_Gate and_1, 32 bits wide
  assign or_1_out = rs1_data | rs2_data;  // OR_Gate or_1, 32 bits wide
  assign xor_1_out = rs1_data ^ rs2_data;  // XOR_Gate xor_1, 32 bits wide
  assign bit_extender_1_out = {{31{1'b0}}, comparator_1_lt};  // Bit_Extender bit_extender_1
  assign bit_extender_2_out = {{31{1'b0}}, comparator_2_lt};  // Bit_Extender bit_extender_2
  Multiplexer #(.select(4), .width(32)) multiplexer_1 (
    .in0(adder_1_out), .in1(subtractor_1_out), .in2(and_1_out), .in3(or_1_out), .in4(xor_1_out),
    .in5(shifter_1_out), .in6(shifter_2_out), .in7(shifter_3_out), .in8(bit_extender_1_out),
    .in9(bit_extender_2_out), .out(result), .sel(ALU_Ctrl));  // open: in10, in11, in12, in13, in14, in15
  // Probe on result

  // Notes on the sheet:
  //   ALU
  //   Every operation is computed in parallel; ALU_Ctrl selects which result leaves the ALU.
  //   ADD   (ctrl 0)
  //   SUB   (ctrl 1)
  //   AND   (ctrl 2)
  //   OR   (ctrl 3)
  //   XOR   (ctrl 4)
  //   SLL (ctrl 5)
  //   SRL (ctrl 6)
  //   SRA (ctrl 7)
  //   SRA: arithmetic shift right
  //   SLT
  //   SLTU
  //   ALU (Arithmetic Logic Unit = khối số học - logic) - tính kết quả theo mã ALUCtrl
  //   Vào: rs1_data = toán hạng A, rs2_data = toán hạng B, ALU_Ctrl = mã phép tính. Ra: result = kết quả 32 bit.
  //   Các lệnh dịch chỉ dùng 5 bit thấp của B (B[4:0], tối đa dịch 31). SRA giữ nguyên bit dấu, SRL chèn bit 0.
  //   ALU_Ctrl  operation
  //   0 ADD   1 SUB   2 AND   3 OR   4 XOR
  //   5 SLL   6 SRL   7 SRA
  //   8 SLT (signed)   9 SLTU (unsigned)
  //   Vì sao tính song song rồi chọn: đơn giản, dễ đọc; tốc độ không quan trọng trong Logisim (không mô phỏng độ trễ cổng).
  //   SLT/SLTU = Set Less Than (đặt 1 nếu A < B, ngược lại 0): SLT so sánh có dấu (-1 < 1), SLTU không dấu (0xFFFFFFFF > 1). Kết quả 1 bit được mở rộng 0 thành 32 bit.
  //   Cách làm: mọi phép tính (cộng, trừ, AND, OR, XOR, dịch trái, dịch phải logic, dịch phải số học, SLT, SLTU) chạy song song; một multiplexer 16 ngả chọn một kết quả theo ALU_Ctrl.
  //   SLT and SLTU: the 1-bit compare result is zero-extended,
  //   so the ALU output is 0x00000000 or 0x00000001.
  //   Các trường hợp: tràn số khi cộng/trừ bị bỏ qua (kết quả quấn vòng 32 bit, đúng theo RISC-V). Mã ALU_Ctrl không dùng (10..15) -> kết quả không xác định, không xảy ra vì ALUControl chỉ sinh 0..9.
endmodule

module InstructionDecode (
  input  [31:0] Instruction,
  output [6:0] funct7,
  output [4:0] rs2,
  output [4:0] rs1,
  output [2:0] funct3,
  output [4:0] rd,
  output [6:0] opcode
);


  assign funct3 = Instruction[14:12];
  assign funct7 = Instruction[31:25];
  assign opcode = Instruction[6:0];
  assign rd = Instruction[11:7];
  assign rs1 = Instruction[19:15];
  assign rs2 = Instruction[24:20];

  // Notes on the sheet:
  //   InstructionDecode
  //   Pure wiring (one splitter): cuts the 32-bit instruction into its RISC-V fields.
  //   Field = instruction bits  ->  used by
  //   opcode = instr[6:0]  ->  MainControl (what kind of instruction)
  //   rd = instr[11:7]  ->  RegisterFile write address
  //   funct3 = instr[14:12]  ->  ALUControl, BranchUnit, Memory
  //   rs1 = instr[19:15]  ->  RegisterFile read address 1
  //   rs2 = instr[24:20]  ->  RegisterFile read address 2
  //   funct7 = instr[31:25]  ->  ALUControl (ADD vs SUB, SRL vs SRA)
  //   GIẢI MÃ LỆNH (InstructionDecode) - cắt lệnh 32 bit thành các trường
  //   opcode = bit 6..0 (7 bit): cho biết lệnh thuộc nhóm nào (cộng trừ, load, store, rẽ nhánh, nhảy...).
  //   Mục đích: tách các trường của lệnh RISC-V ra thành các dây riêng để các khối sau dùng (đọc thanh ghi, điều khiển, ALU).
  //   Viết tắt: opcode = Operation Code (mã thao tác); rd = Destination Register (thanh ghi đích); rs1, rs2 = Source Register 1, 2 (thanh ghi nguồn).
  //   rd = bit 11..7 (5 bit): số thanh ghi sẽ được ghi kết quả (x0..x31).   funct3 = bit 14..12 (3 bit): chọn biến thể trong nhóm (vd beq/bne/blt).
  //   rs1 = bit 19..15, rs2 = bit 24..20 (5 bit mỗi trường): số thanh ghi cần đọc.   funct7 = bit 31..25 (7 bit): phân biệt ADD/SUB, SRL/SRA.
  //   Các trường hợp: lệnh kiểu U (lui, auipc) và J (jal) không có rs1/rs2/funct3 thật; các bit đó vẫn được cắt ra nhưng các khối sau bỏ qua.
  //   Vì sao không có cổng logic: RISC-V đặt các trường ở vị trí cố định, nên giải mã chỉ là đi dây (một splitter), rất nhanh và rẻ.
endmodule

module RegisterFile (
  input  [31:0] write_data,
  input  CLK,
  input  write,
  input  [4:0] rd,
  input  [4:0] rs1,
  input  [4:0] rs2,
  output [31:0] rs1_data,
  output [31:0] rs2_data
);

  wire demultiplexer_1_out0, WE0, WE1, WE2, WE3, WE4, WE5, WE6, WE7, WE8, WE9, WE10, WE11, WE12, WE13, WE14,
       WE15, WE16, WE17, WE18, WE19, WE20, WE21, WE22, WE23, WE24, WE25, WE26, WE27, WE28, WE29, WE30, WE31;
  wire [31:0] X0, X1, X2, X3, X4, X5, X6, X7, X8, X9, X10, X11, X12, X13, X14, X15, X16, X17, X18, X19, X20,
       X21, X22, X23, X24, X25, X26, X27, X28, X29, X30, X31;

  Register #(.width(32)) u_x0 (.D({32{1'b0}}), .en(WE0), .clk(CLK), .Q(X0));  // open: clr
  Register #(.width(32)) u_x1 (.D(write_data), .en(WE1), .clk(CLK), .Q(X1));  // open: clr
  Register #(.width(32)) u_x2 (.D(write_data), .en(WE2), .clk(CLK), .Q(X2));  // open: clr
  Register #(.width(32)) u_x3 (.D(write_data), .en(WE3), .clk(CLK), .Q(X3));  // open: clr
  Register #(.width(32)) u_x4 (.D(write_data), .en(WE4), .clk(CLK), .Q(X4));  // open: clr
  Register #(.width(32)) u_x5 (.D(write_data), .en(WE5), .clk(CLK), .Q(X5));  // open: clr
  Register #(.width(32)) u_x6 (.D(write_data), .en(WE6), .clk(CLK), .Q(X6));  // open: clr
  Register #(.width(32)) u_x7 (.D(write_data), .en(WE7), .clk(CLK), .Q(X7));  // open: clr
  Multiplexer #(.select(5), .width(32)) multiplexer_1 (
    .in0(X0), .in1(X1), .in2(X2), .in3(X3), .in4(X4), .in5(X5), .in6(X6), .in7(X7), .in8(X8), .in9(X9),
    .in10(X10), .in11(X11), .in12(X12), .in13(X13), .in14(X14), .in15(X15), .in16(X16), .in17(X17),
    .in18(X18), .in19(X19), .in20(X20), .in21(X21), .in22(X22), .in23(X23), .in24(X24), .in25(X25),
    .in26(X26), .in27(X27), .in28(X28), .in29(X29), .in30(X30), .in31(X31), .out(rs1_data), .sel(rs1));
  Register #(.width(32)) u_x8 (.D(write_data), .en(WE8), .clk(CLK), .Q(X8));  // open: clr
  Register #(.width(32)) u_x9 (.D(write_data), .en(WE9), .clk(CLK), .Q(X9));  // open: clr
  Register #(.width(32)) u_x10 (.D(write_data), .en(WE10), .clk(CLK), .Q(X10));  // open: clr
  Register #(.width(32)) u_x11 (.D(write_data), .en(WE11), .clk(CLK), .Q(X11));  // open: clr
  Register #(.width(32)) u_x12 (.D(write_data), .en(WE12), .clk(CLK), .Q(X12));  // open: clr
  Register #(.width(32)) u_x13 (.D(write_data), .en(WE13), .clk(CLK), .Q(X13));  // open: clr
  Register #(.width(32)) u_x14 (.D(write_data), .en(WE14), .clk(CLK), .Q(X14));  // open: clr
  Register #(.width(32)) u_x15 (.D(write_data), .en(WE15), .clk(CLK), .Q(X15));  // open: clr
  Multiplexer #(.select(5), .width(32)) multiplexer_2 (
    .in0(X0), .in1(X1), .in2(X2), .in3(X3), .in4(X4), .in5(X5), .in6(X6), .in7(X7), .in8(X8), .in9(X9),
    .in10(X10), .in11(X11), .in12(X12), .in13(X13), .in14(X14), .in15(X15), .in16(X16), .in17(X17),
    .in18(X18), .in19(X19), .in20(X20), .in21(X21), .in22(X22), .in23(X23), .in24(X24), .in25(X25),
    .in26(X26), .in27(X27), .in28(X28), .in29(X29), .in30(X30), .in31(X31), .out(rs2_data), .sel(rs2));
  Register #(.width(32)) u_x16 (.D(write_data), .en(WE16), .clk(CLK), .Q(X16));  // open: clr
  Register #(.width(32)) u_x17 (.D(write_data), .en(WE17), .clk(CLK), .Q(X17));  // open: clr
  Register #(.width(32)) u_x18 (.D(write_data), .en(WE18), .clk(CLK), .Q(X18));  // open: clr
  Register #(.width(32)) u_x19 (.D(write_data), .en(WE19), .clk(CLK), .Q(X19));  // open: clr
  Register #(.width(32)) u_x20 (.D(write_data), .en(WE20), .clk(CLK), .Q(X20));  // open: clr
  Register #(.width(32)) u_x21 (.D(write_data), .en(WE21), .clk(CLK), .Q(X21));  // open: clr
  Register #(.width(32)) u_x22 (.D(write_data), .en(WE22), .clk(CLK), .Q(X22));  // open: clr
  Register #(.width(32)) u_x23 (.D(write_data), .en(WE23), .clk(CLK), .Q(X23));  // open: clr
  Demultiplexer #(.select(5)) demultiplexer_1 (
    .out0(demultiplexer_1_out0), .out1(WE1), .out2(WE2), .out3(WE3), .out4(WE4), .out5(WE5), .out6(WE6),
    .out7(WE7), .out8(WE8), .out9(WE9), .out10(WE10), .out11(WE11), .out12(WE12), .out13(WE13), .out14(WE14),
    .out15(WE15), .out16(WE16), .out17(WE17), .out18(WE18), .out19(WE19), .out20(WE20), .out21(WE21),
    .out22(WE22), .out23(WE23), .out24(WE24), .out25(WE25), .out26(WE26), .out27(WE27), .out28(WE28),
    .out29(WE29), .out30(WE30), .out31(WE31), .in(write), .sel(rd));
  Register #(.width(32)) u_x24 (.D(write_data), .en(WE24), .clk(CLK), .Q(X24));  // open: clr
  Register #(.width(32)) u_x25 (.D(write_data), .en(WE25), .clk(CLK), .Q(X25));  // open: clr
  Register #(.width(32)) u_x26 (.D(write_data), .en(WE26), .clk(CLK), .Q(X26));  // open: clr
  Register #(.width(32)) u_x27 (.D(write_data), .en(WE27), .clk(CLK), .Q(X27));  // open: clr
  Register #(.width(32)) u_x28 (.D(write_data), .en(WE28), .clk(CLK), .Q(X28));  // open: clr
  Register #(.width(32)) u_x29 (.D(write_data), .en(WE29), .clk(CLK), .Q(X29));  // open: clr
  Register #(.width(32)) u_x30 (.D(write_data), .en(WE30), .clk(CLK), .Q(X30));  // open: clr
  Register #(.width(32)) u_x31 (.D(write_data), .en(WE31), .clk(CLK), .Q(X31));  // open: clr

  // Other names for the same wires on the sheet: wb_data[31:0] = write_data

  // Notes on the sheet:
  //   TẬP THANH GHI (RegisterFile) - 32 thanh ghi x0..x31, mỗi thanh ghi 32 bit
  //   Vì sao 32 thanh ghi riêng + mux: mỗi thanh ghi là một hộp có nhãn, nhìn thấy được trong tab State của Logisim.
  //   Đọc: hai cổng đọc độc lập (rs1 -> rs1_data, rs2 -> rs2_data), đọc bất đồng bộ (đổi số thanh ghi là giá trị ra ngay, không chờ xung).
  //   Read port 1: x[rs1] -> rs1_data
  //   Viết tắt: x0..x31 = 32 thanh ghi của RISC-V; rd = thanh ghi đích; rs1/rs2 = thanh ghi nguồn; write = RegWrite (cho phép ghi); CLK = xung nhịp.
  //   Ghi: nếu write = 1 thì ở cạnh xung nhịp, write_data được ghi vào thanh ghi số rd (bộ DEMUX bật tín hiệu cho phép ghi của đúng một thanh ghi).
  //   Trong pipeline: khối này nhận xung nhịp ĐẢO (CLK_n) nên ghi ở cạnh xuống: lệnh ở WB ghi nửa đầu chu kỳ, lệnh ở ID đọc nửa sau -> thấy giá trị mới.
  //   Các trường hợp: write = 0 -> không thanh ghi nào đổi (store, branch). rd = 0 -> x0 không đổi, luôn bằng 0 (hằng số 0). Đọc và ghi cùng thanh ghi trong một chu kỳ -> đọc giá trị cũ.
  //   RegisterFile
  //   32 registers x 32 bits. x0 always loads the constant 0, so it always reads 0.
  //   Write: wb_data goes to every register; the DMX turns on only WE[rd] when write = 1.
  //   Read: two 32:1 multiplexers pick x[rs1] and x[rs2] (asynchronous, no clock needed).
  //   Read port 2: x[rs2] -> rs2_data
  //   Write decoder: rd -> WE of one register
endmodule

module ImmGen (
  input  [31:0] Instruction,
  input  [2:0] ImmSel,
  output [31:0] Imm
);

  wire [31:0] bit_extender_1_out, bit_extender_2_out, bit_extender_3_out, bit_extender_4_out;

  assign bit_extender_1_out = {{20{Instruction[31]}}, Instruction[31:20]};  // Bit_Extender bit_extender_1
  assign bit_extender_2_out = {{20{Instruction[31]}}, {Instruction[31:25], Instruction[11:7]}};  // Bit_Extender bit_extender_2
  assign bit_extender_3_out = {{19{Instruction[31]}}, {Instruction[31], Instruction[7], Instruction[30:25], Instruction[11:8], 1'b0}};  // Bit_Extender bit_extender_3
  assign bit_extender_4_out = {{11{Instruction[31]}}, {Instruction[31], Instruction[19:12], Instruction[20], Instruction[30:21], 1'b0}};  // Bit_Extender bit_extender_4
  Multiplexer #(.select(3), .width(32)) multiplexer_1 (
    .in0(bit_extender_1_out), .in1(bit_extender_2_out), .in2(bit_extender_3_out),
    .in3({Instruction[31:12], {12{1'b0}}}), .in4(bit_extender_4_out), .out(Imm), .sel(ImmSel));  // open: in5, in6, in7

  // Notes on the sheet:
  //   imm = instr[31:20]
  //   imm = instr[31:25], instr[11:7]
  //   imm = instr[31], [7], [30:25], [11:8], 0
  //   imm = instr[31:12] << 12
  //   low 12 bits are zero (12 zero bits appended)
  //   imm = instr[31], [19:12], [20], [30:21], 0
  //   bit 0 is always 0 (offsets are even)
  //   I-type
  //   S-type
  //   B-type
  //   U-type
  //   J-type
  //   SINH HẰNG SỐ (ImmGen = Immediate Generator) - dựng hằng số tức thời 32 bit
  //   Viết tắt: imm = immediate = hằng số nằm ngay trong lệnh (không phải đọc từ thanh ghi).
  //   ImmGen
  //   Rebuilds the 32-bit immediate from the instruction bits; ImmSel picks the format.
  //   Các trường hợp: B và J luôn chẵn (bit 0 = 0) vì lệnh dài 4 byte; U không mở rộng dấu mà chèn 12 bit 0 vào cuối.
  //   Mục đích: mỗi kiểu lệnh cất hằng số ở chỗ khác nhau và bị xáo bit; khối này gom lại đúng thứ tự rồi mở rộng dấu thành 32 bit.
  //   Mở rộng dấu (sign extension): bit cao nhất của hằng số được chép vào các bit trên, nên số âm vẫn âm (vd -8 = 0xFFFFFFF8).
  //   Vì sao xáo bit: để bit dấu luôn ở bit 31 của lệnh và nhiều bit nằm cùng vị trí giữa các kiểu, nên mạch giải mã đơn giản hơn.
  //   ImmSel chọn kiểu: 000 I (addi, load, jalr: 12 bit), 001 S (store: 12 bit), 010 B (branch: 13 bit, bit 0 = 0), 011 U (lui, auipc: imm << 12), 100 J (jal: 21 bit, bit 0 = 0).
  //   ImmSel: 0 I   1 S   2 B   3 U   4 J
  //   All results are sign-extended to 32 bits.
endmodule

module MainControl (
  input  [6:0] opcode,
  output RegWrite,
  output ALUSrc,
  output MemWrite,
  output MemRead,
  output IsBranch,
  output [1:0] ALUOp,
  output [2:0] ImmSel,
  output [1:0] ASel,
  output [1:0] WBSel,
  output IsJAL,
  output IsJALR
);

  wire as_a, as_b, IsI, IsR, rw_a, rw_b;

  Comparator #(.mode("unsigned"), .width(7)) comparator_1 (.a(opcode), .b(7'b0110011), .eq(IsR));  // open: gt, lt
  Comparator #(.mode("unsigned"), .width(7)) comparator_2 (.a(opcode), .b(7'b0010011), .eq(IsI));  // open: gt, lt
  Comparator #(.mode("unsigned"), .width(7)) comparator_3 (.a(opcode), .b(7'b0000011), .eq(MemRead));  // open: gt, lt
  Comparator #(.mode("unsigned"), .width(7)) comparator_4 (.a(opcode), .b(7'b0100011), .eq(MemWrite));  // open: gt, lt
  Comparator #(.mode("unsigned"), .width(7)) comparator_5 (.a(opcode), .b(7'b1100011), .eq(IsBranch));  // open: gt, lt
  Comparator #(.mode("unsigned"), .width(7)) comparator_6 (.a(opcode), .b(7'b0110111), .eq(ASel[1]));  // open: gt, lt
  Comparator #(.mode("unsigned"), .width(7)) comparator_7 (.a(opcode), .b(7'b0010111), .eq(ASel[0]));  // open: gt, lt
  Comparator #(.mode("unsigned"), .width(7)) comparator_8 (.a(opcode), .b(7'b1101111), .eq(ImmSel[2]));  // open: gt, lt
  Comparator #(.mode("unsigned"), .width(7)) comparator_9 (.a(opcode), .b(7'b1100111), .eq(IsJALR));  // open: gt, lt
  or or_1 (rw_a, IsR, IsI, MemRead);
  or or_2 (rw_b, ASel[1], ASel[0], ImmSel[2]);
  or or_3 (as_a, IsI, MemRead, MemWrite);
  or or_4 (as_b, ASel[1], ASel[0], IsJALR);
  or or_5 (ALUOp[0], IsI, IsBranch);
  or or_6 (ALUOp[1], IsR, IsI);
  or or_7 (ImmSel[0], MemWrite, ASel[1], ASel[0]);
  or or_8 (ImmSel[1], IsBranch, ASel[1], ASel[0]);
  or or_9 (WBSel[1], ImmSel[2], IsJALR);
  or or_10 (RegWrite, rw_a, rw_b, IsJALR);
  or or_11 (ALUSrc, as_a, as_b);

  assign IsJAL = ImmSel[2];
  assign WBSel[0] = MemRead;

  // Other names for the same wires on the sheet: IsAuipc = ASel[0]; IsLui = ASel[1]; IsStore = MemWrite;
  //   IsLoad = MemRead

  // Notes on the sheet:
  //   opcode 0x13 = I-type ALU
  //   opcode 0x23 = store
  //   opcode 0x37 = LUI
  //   opcode 0x6F = JAL
  //   opcode 0x67 = JALR
  //   opcode 0x33 = R-type
  //   opcode 0x03 = load
  //   opcode 0x63 = branch
  //   opcode 0x17 = AUIPC
  //   MainControl
  //   Compares opcode with each instruction class (left) and combines the flags into control signals (right).
  //   ĐIỀU KHIỂN CHÍNH (MainControl) - từ opcode sinh mọi tín hiệu điều khiển
  //   WBSel (2 bit) = giá trị ghi vào rd: 00 kết quả ALU, 01 dữ liệu RAM (load), 10 PC+4 (jal, jalr = địa chỉ trả về).
  //   ImmSel (3 bit) = kiểu hằng số: 000 I, 001 S, 010 B, 011 U, 100 J.   ASel (2 bit) = toán hạng A: 00 rs1, 01 PC (auipc), 10 số 0 (lui).
  //   Vì sao so sánh từng opcode: mỗi dòng của bảng opcode hiện ra thành một bộ so sánh, dễ đọc và dễ kiểm tra (tests/maincontrol.vec).
  //   Viết tắt: RegWrite = ghi thanh ghi; ALUSrc = nguồn của toán hạng B; MemWrite/MemRead = ghi/đọc RAM; IsBranch/IsJAL/IsJALR = lệnh rẽ nhánh/nhảy.
  //   ALUOp (2 bit) = nhóm phép ALU: 00 cộng (load, store, lui, auipc, jalr), 01 trừ (branch), 10 kiểu R, 11 kiểu I (ALUControl chọn tiếp theo funct3/funct7).
  //   Các trường hợp: opcode lạ (không thuộc 9 nhóm) -> mọi tín hiệu = 0, lệnh không làm gì (NOP an toàn). store/branch không ghi thanh ghi (RegWrite = 0).
  //   Cách làm: 9 bộ so sánh 7 bit (mỗi opcode một cái) cho ra cờ của từng nhóm lệnh; cổng OR gộp cờ thành tín hiệu: vd RegWrite = R hoặc I hoặc load hoặc lui hoặc auipc hoặc jal hoặc jalr.
  //   WBSel (value written to rd): 00 ALU result   01 memory   10 PC + 4 (JAL, JALR)
  //   RegWrite: every class that writes rd
  //   ALUSrc = 1: ALU operand B is the immediate
  //   ALUOp: 00 add (load/store/LUI/AUIPC/jumps)  01 sub (branch)  10 R-type  11 I-type
  //   ImmSel: 000 I   001 S (store)   010 B (branch)   011 U (LUI, AUIPC)   100 J (JAL)
  //   ASel (ALU operand A): 00 rs1   01 PC (AUIPC)   10 zero (LUI)
endmodule

module ALUControl (
  input  [6:0] funct7,
  input  [1:0] ALUOp,
  input  [2:0] funct3,
  output [3:0] ALUCtrl
);

  wire [3:0] multiplexer_1_out, multiplexer_2_out, multiplexer_3_out, multiplexer_4_out;

  Multiplexer #(.width(4)) multiplexer_1 (.in0(4'b0110), .in1(4'b0111), .out(multiplexer_1_out), .sel(funct7[5]));
  Multiplexer #(.width(4)) multiplexer_2 (.in0(4'b0000), .in1(4'b0001), .out(multiplexer_2_out), .sel(funct7[5]));
  Multiplexer #(.select(3), .width(4)) multiplexer_3 (
    .in0(multiplexer_2_out), .in1(4'b0101), .in2(4'b1000), .in3(4'b1001), .in4(4'b0100),
    .in5(multiplexer_1_out), .in6(4'b0011), .in7(4'b0010), .out(multiplexer_3_out), .sel(funct3));
  Multiplexer #(.select(3), .width(4)) multiplexer_4 (
    .in0(4'b0000), .in1(4'b0101), .in2(4'b1000), .in3(4'b1001), .in4(4'b0100), .in5(multiplexer_1_out),
    .in6(4'b0011), .in7(4'b0010), .out(multiplexer_4_out), .sel(funct3));
  Multiplexer #(.select(2), .width(4)) multiplexer_5 (
    .in0(4'b0000), .in1(4'b0001), .in2(multiplexer_3_out), .in3(multiplexer_4_out), .out(ALUCtrl), .sel(ALUOp));

  // Notes on the sheet:
  //   ADDI 0000
  //   SLLI 0101
  //   SLTI 1000
  //   SLTIU 1001
  //   XORI 0100
  //   ANDI 0010
  //   ORI 0011
  //   SRL 0110
  //   SRA 0111
  //   ADD 0000
  //   SUB 0001
  //   SLL 0101
  //   SLT 1000
  //   SLTU 1001
  //   XOR 0100
  //   OR 0011
  //   AND 0010
  //   ALUControl
  //   ALUOp 00 = ADD (load/store)   01 = SUB (branch)   10 = R-type   11 = I-type
  //   R-type and I-type pick the operation from funct3 (funct7 separates ADD/SUB and SRL/SRA).
  //   ĐIỀU KHIỂN ALU (ALUControl) - đổi ALUOp, funct3, funct7 thành mã ALUCtrl 4 bit
  //   Viết tắt: ALU = Arithmetic Logic Unit (khối số học - logic); ALUCtrl = mã chọn phép tính của ALU.
  //   Vì sao hai tầng điều khiển (MainControl -> ALUOp -> ALUControl): mỗi bảng nhỏ, kiểm thử riêng được (tests/alucontrol.vec).
  //   R-dec
  //   Mã ALUCtrl: 0 ADD (cộng), 1 SUB (trừ), 2 AND, 3 OR, 4 XOR, 5 SLL (dịch trái), 6 SRL (dịch phải logic), 7 SRA (dịch phải số học), 8 SLT (so sánh có dấu), 9 SLTU (không dấu).
  //   ALUOp = 00 -> luôn ADD (tính địa chỉ load/store, lui, auipc, jalr). ALUOp = 01 -> luôn SUB (so sánh cho branch). ALUOp = 10 -> tra bảng kiểu R. ALUOp = 11 -> tra bảng kiểu I.
  //   Kiểu R: funct3 chọn phép; funct7 bit 5 = 1 biến ADD thành SUB và SRL thành SRA. Kiểu I: chỉ lệnh dịch (slli, srli, srai) xét funct7 bit 5; addi bỏ qua funct7.
endmodule

module Memory (
  input  [31:0] Address,
  input  [31:0] write_data,
  input  MemWrite,
  input  CLK,
  input  [2:0] funct3,
  output [31:0] read_data
);

  wire [31:0] wnew, word;

  RAM #(.addrWidth(8), .asyncread("true"), .dataWidth(32), .enables("line")) ram_1 (
    .addr(Address[9:2]), .we(MemWrite), .clk(CLK), .din(wnew), .dout(word));
  StoreMerge storemerge_1 (
    .old_word(word), .write_data(write_data), .funct3(funct3), .boff(Address[1:0]), .new_word(wnew));
  LoadExtract loadextract_1 (.word(word), .boff(Address[1:0]), .funct3(funct3), .read_data(read_data));

  // Other names for the same wires on the sheet: boff[1:0] = Address[1:0]; widx[7:0] = Address[9:2]

  // Notes on the sheet:
  //   Address[1:0] = byte in the word, Address[9:2] = word index
  //   BỘ NHỚ DỮ LIỆU (Memory) - RAM 256 từ x 32 bit cùng LoadExtract và StoreMerge
  //   Data RAM 256 x 32 with asynchronous read.  Loads: lb lh lw lbu lhu.  Stores: sb sh sw (read-modify-write of one word).
  //   Memory
  //   RAM: writes on the clock edge when MemWrite = 1
  //   Viết tắt: RAM = Random Access Memory (bộ nhớ đọc ghi, mất dữ liệu khi tắt). Address[9:2] = chỉ số từ (0..255), Address[1:0] = byte trong từ.
  //   Đọc: bất đồng bộ - địa chỉ vừa đổi là dữ liệu ra ngay trong cùng chu kỳ (lệnh load cần vậy). Ghi: chỉ khi MemWrite = 1, ở cạnh lên của xung nhịp.
  //   Vì sao RAM đọc bất đồng bộ: RAM đọc đồng bộ chỉ trả dữ liệu sau cạnh xung kế tiếp; khi đó load trả dữ liệu không xác định (lỗi đã gặp và sửa).
  //   Vào: Address (địa chỉ từ ALU), write_data (dữ liệu của lệnh store), MemWrite (cho phép ghi), CLK (xung nhịp), funct3 (loại load/store). Ra: read_data (dữ liệu cho lệnh load).
  //   Các trường hợp: lệnh không phải load/store -> MemWrite = 0 nên RAM không đổi; read_data vẫn có giá trị nhưng bị bỏ qua. Địa chỉ >= 1 KiB quấn vòng (chỉ dùng Address[9:2]).
  //   StoreMerge: new word to write
  //   LoadExtract: value delivered to the CPU
endmodule

module BranchUnit (
  input  [31:0] rs1_data,
  input  [31:0] rs2_data,
  input  IsBranch,
  input  [2:0] funct3,
  output branch_taken
);

  wire cond, eq, ges, geu, lts, ltu, ne;

  Comparator #(.mode("unsigned"), .width(32)) comparator_1 (.a(rs1_data), .b(rs2_data), .eq(eq), .lt(ltu));  // open: gt
  Comparator #(.width(32)) comparator_2 (.a(rs1_data), .b(rs2_data), .lt(lts));  // open: gt, eq
  not not_1 (ne, eq);
  not not_2 (geu, ltu);
  not not_3 (ges, lts);
  Multiplexer #(.select(3), .width(1)) multiplexer_1 (
    .in0(eq), .in1(ne), .in2(1'b0), .in3(1'b0), .in4(lts), .in5(ges), .in6(ltu), .in7(geu), .out(cond),
    .sel(funct3));
  and and_1 (branch_taken, IsBranch, cond);

  // Notes on the sheet:
  //   BranchUnit
  //   Decides whether a conditional branch is taken: funct3 picks the comparison, IsBranch enables it.
  //   Khi branch_taken = 1, PC kế tiếp = PC + hằng số B (xem mạch main / Pipeline).
  //   ĐƠN VỊ RẼ NHÁNH (BranchUnit) - quyết định lệnh rẽ nhánh có được rẽ không
  //   unsigned compare
  //   signed compare
  //   Vào: rs1_data, rs2_data (hai giá trị cần so), IsBranch (đây có phải lệnh branch), funct3 (chọn phép so). Ra: branch_taken = 1 nếu phải rẽ.
  //   Các trường hợp: funct3 = 010 hoặc 011 (không có lệnh branch như vậy) -> điều kiện = 0, không rẽ. IsBranch = 0 (lệnh khác) -> branch_taken = 0 dù hai giá trị thế nào.
  //   Cách làm: một bộ so sánh không dấu và một có dấu cho ra '=', '<'; cổng NOT cho ra '!=', '>='; multiplexer theo funct3 chọn điều kiện: 000 beq, 001 bne, 100 blt, 101 bge, 110 bltu, 111 bgeu.
  //   Viết tắt: beq = branch if equal (rẽ nếu bằng); bne = not equal (khác); blt = less than (nhỏ hơn, có dấu); bge = greater or equal (lớn hơn hoặc bằng, có dấu); bltu/bgeu = như blt/bge nhưng không dấu.
  //   funct3: 000 beq  001 bne  100 blt  101 bge  110 bltu  111 bgeu
endmodule

module LoadExtract (
  input  [31:0] word,
  input  [1:0] boff,
  input  [2:0] funct3,
  output [31:0] read_data
);

  wire [7:0] ldbyte;
  wire [15:0] ldhalf;
  wire [31:0] lb, lbu, lh, lhu;

  Multiplexer #(.select(2), .width(8)) multiplexer_1 (
    .in0(word[7:0]), .in1(word[15:8]), .in2(word[23:16]), .in3(word[31:24]), .out(ldbyte), .sel(boff));
  Multiplexer #(.select(1), .width(16)) multiplexer_2 (
    .in0(word[15:0]), .in1(word[31:16]), .out(ldhalf), .sel(boff[1]));
  assign lb = {{24{ldbyte[7]}}, ldbyte};  // Bit_Extender bit_extender_1
  assign lbu = {{24{1'b0}}, ldbyte};  // Bit_Extender bit_extender_2
  assign lh = {{16{ldhalf[15]}}, ldhalf};  // Bit_Extender bit_extender_3
  assign lhu = {{16{1'b0}}, ldhalf};  // Bit_Extender bit_extender_4
  Multiplexer #(.select(3), .width(32)) multiplexer_3 (
    .in0(lb), .in1(lh), .in2(word), .in3(word), .in4(lbu), .in5(lhu), .in6(word), .in7(word),
    .out(read_data), .sel(funct3));

  // Other names for the same wires on the sheet: by0[7:0] = word[7:0]; hw0[15:0] = word[15:0]; by1[7:0] = word[15:8];
  //   by2[7:0] = word[23:16]; hw1[15:0] = word[31:16]; by3[7:0] = word[31:24]

  // Notes on the sheet:
  //   Picks the loaded byte / halfword out of the 32-bit word and extends it: lb lh lw lbu lhu.
  //   LoadExtract
  //   TRÍCH DỮ LIỆU LOAD (LoadExtract) - lấy byte / nửa từ ra khỏi từ 32 bit và mở rộng
  //   funct3: 000 lb, 001 lh, 010 lw, 100 lbu, 101 lhu. Byte được chọn bằng Address[1:0], nửa từ bằng Address[1].
  //   Vì sao cần khối này: RAM của dự án đọc nguyên từ 32 bit, nên việc cắt byte/nửa từ phải làm riêng.
  //   byte selected by Address[1:0]
  //   halfword selected by Address[1]
  //   Vào: dữ liệu cả từ đọc từ RAM, Address[1:0] (byte nào trong từ), funct3 (loại lệnh load). Ra: giá trị 32 bit đưa về thanh ghi.
  //   Các trường hợp: lb với byte 0x80 -> 0xFFFFFF80 (mở rộng dấu), lbu cùng byte -> 0x00000080. lw lấy nguyên từ, không cần mở rộng.
  //   Viết tắt: lb = load byte (nạp 1 byte, mở rộng dấu); lh = load halfword (nửa từ 16 bit, mở rộng dấu); lw = load word (cả từ 32 bit); lbu/lhu = như lb/lh nhưng mở rộng 0 (không dấu).
  //   funct3: 000 lb  001 lh  010 lw  100 lbu  101 lhu
endmodule

module StoreMerge (
  input  [31:0] old_word,
  input  [31:0] write_data,
  input  [2:0] funct3,
  input  [1:0] boff,
  output [31:0] new_word
);

  wire [3:0] en;
  wire [7:0] src1, src2, src3;

  Multiplexer #(.select(2), .width(8)) multiplexer_1 (
    .in0(write_data[7:0]), .in1(write_data[15:8]), .in2(write_data[15:8]), .in3(write_data[15:8]),
    .out(src1), .sel(funct3[1:0]));
  Multiplexer #(.select(2), .width(8)) multiplexer_2 (
    .in0(write_data[7:0]), .in1(write_data[7:0]), .in2(write_data[23:16]), .in3(write_data[23:16]),
    .out(src2), .sel(funct3[1:0]));
  Multiplexer #(.select(2), .width(8)) multiplexer_3 (
    .in0(write_data[7:0]), .in1(write_data[15:8]), .in2(write_data[31:24]), .in3(write_data[31:24]),
    .out(src3), .sel(funct3[1:0]));
  ROM #(.addrWidth(4), .dataWidth(4)) rom_1 (.addr({funct3[1:0], boff}), .data(en));
  Multiplexer #(.select(1), .width(8)) multiplexer_4 (
    .in0(old_word[7:0]), .in1(write_data[7:0]), .out(new_word[7:0]), .sel(en[0]));
  Multiplexer #(.select(1), .width(8)) multiplexer_5 (
    .in0(old_word[15:8]), .in1(src1), .out(new_word[15:8]), .sel(en[1]));
  Multiplexer #(.select(1), .width(8)) multiplexer_6 (
    .in0(old_word[23:16]), .in1(src2), .out(new_word[23:16]), .sel(en[2]));
  Multiplexer #(.select(1), .width(8)) multiplexer_7 (
    .in0(old_word[31:24]), .in1(src3), .out(new_word[31:24]), .sel(en[3]));

  // Other names for the same wires on the sheet: enaddr[3:0] = {funct3[1:0], boff}; size[1:0] = funct3[1:0];
  //   nb0[7:0] = new_word[7:0]; nb1[7:0] = new_word[15:8]; nb2[7:0] = new_word[23:16]; nb3[7:0] = new_word[31:24];
  //   ob0[7:0] = old_word[7:0]; ob1[7:0] = old_word[15:8]; ob2[7:0] = old_word[23:16]; ob3[7:0] = old_word[31:24];
  //   wd0[7:0] = write_data[7:0]; wd1[7:0] = write_data[15:8]; wd2[7:0] = write_data[23:16];
  //   wd3[7:0] = write_data[31:24]

  // Notes on the sheet:
  //   size = funct3[1:0]: 00 byte  01 half  10 word
  //   Ví dụ: từ cũ 0x11223344, sb 0xAA vào byte 1 -> từ mới 0x1122AA44.
  //   GHÉP DỮ LIỆU STORE (StoreMerge) - tạo từ mới để ghi vào RAM (đọc - sửa - ghi)
  //   A store writes a whole RAM word, so keep the old bytes that are not written: sb, sh, sw.
  //   StoreMerge
  //   source byte for lane 1 / 2 / 3
  //   Vấn đề: RAM chỉ ghi nguyên từ 32 bit. Nên khi ghi 1 byte phải giữ lại 3 byte cũ: đọc từ cũ, thay đúng làn byte, ghi cả từ trở lại.
  //   Các trường hợp: sw -> cả 4 làn lấy dữ liệu mới. sb vào byte 1 -> chỉ làn 1 lấy byte thấp của write_data, các làn khác giữ byte cũ. sh -> 2 làn.
  //   Viết tắt: sb = store byte (ghi 1 byte); sh = store halfword (ghi nửa từ); sw = store word (ghi cả từ). size = độ rộng lệnh store (funct3[1:0]): 00 byte, 01 nửa từ, 10 từ.
  //   byte enables: row = {size, Address[1:0]}
  //   contents of rom_1 (hex, n*v repeats v):
  //   1 2 4 8 3 3 c c f f f f f f f f
  //   byte 0001 0010 0100 1000 | half 0011 0011 1100 1100 | word 1111
  //   Cách làm: ROM 16 hàng x 4 bit đổi {size, Address[1:0]} thành 4 bit cho phép từng làn byte (byte: 0001 0010 0100 1000, nửa từ: 0011 1100, từ: 1111). Mỗi làn chọn byte mới hoặc byte cũ.
  //   lane i = enable ? new byte : old byte
endmodule

module ForwardingUnit (
  input  [4:0] rs1_ex,
  input  [4:0] rs2_ex,
  input  [4:0] rd_mem,
  input  RegWrite_mem,
  input  [4:0] rd_wb,
  input  RegWrite_wb,
  output [1:0] ForwardA,
  output [1:0] ForwardB
);

  wire mem_eq_A, mem_eq_B, mem_is_x0, mem_ok0, mem_valid, not_mem_A, not_mem_B, wb_eq_A, wb_eq_B, wb_hit_A,
       wb_hit_B, wb_is_x0, wb_ok0, wb_valid;

  Comparator #(.mode("unsigned"), .width(5)) comparator_1 (.a(rd_mem), .b({5{1'b0}}), .eq(mem_is_x0));  // open: gt, lt
  Comparator #(.mode("unsigned"), .width(5)) comparator_2 (.a(rd_wb), .b({5{1'b0}}), .eq(wb_is_x0));  // open: gt, lt
  Comparator #(.mode("unsigned"), .width(5)) comparator_3 (.a(rd_mem), .b(rs1_ex), .eq(mem_eq_A));  // open: gt, lt
  Comparator #(.mode("unsigned"), .width(5)) comparator_4 (.a(rd_wb), .b(rs1_ex), .eq(wb_eq_A));  // open: gt, lt
  Comparator #(.mode("unsigned"), .width(5)) comparator_5 (.a(rd_mem), .b(rs2_ex), .eq(mem_eq_B));  // open: gt, lt
  Comparator #(.mode("unsigned"), .width(5)) comparator_6 (.a(rd_wb), .b(rs2_ex), .eq(wb_eq_B));  // open: gt, lt
  not not_1 (mem_ok0, mem_is_x0);
  not not_2 (wb_ok0, wb_is_x0);
  and and_1 (mem_valid, RegWrite_mem, mem_ok0);
  and and_2 (wb_valid, RegWrite_wb, wb_ok0);
  and and_3 (ForwardA[1], mem_valid, mem_eq_A);
  and and_4 (wb_hit_A, wb_valid, wb_eq_A);
  and and_5 (ForwardB[1], mem_valid, mem_eq_B);
  and and_6 (wb_hit_B, wb_valid, wb_eq_B);
  not not_3 (not_mem_A, ForwardA[1]);
  not not_4 (not_mem_B, ForwardB[1]);
  and and_7 (ForwardA[0], wb_hit_A, not_mem_A);
  and and_8 (ForwardB[0], wb_hit_B, not_mem_B);

  // Other names for the same wires on the sheet: from_wb_A = ForwardA[0]; from_mem_A = ForwardA[1];
  //   from_wb_B = ForwardB[0]; from_mem_B = ForwardB[1]

  // Notes on the sheet:
  //   ForwardingUnit
  //   Pipeline data hazards: take an operand of the EX stage from a later stage instead of the register file.
  //   ĐƠN VỊ CHUYỂN TIẾP (ForwardingUnit) - lấy toán hạng mới nhất cho tầng EX
  //   operand A (rs1): EX/MEM has priority over MEM/WB
  //   operand B (rs2)
  //   Vấn đề: lệnh trước chưa kịp ghi vào register file thì lệnh sau đã cần dùng giá trị đó (phụ thuộc dữ liệu, RAW = Read After Write).
  //   Forward = 10: lấy từ EX/MEM (lệnh ngay trước). Forward = 01: lấy từ MEM/WB (lệnh cách một). Forward = 00: lấy từ register file (không phụ thuộc).
  //   Viết tắt: forwarding = chuyển tiếp (bypass): đưa kết quả từ tầng sau về tầng EX mà không chờ ghi vào thanh ghi. EX/MEM, MEM/WB = thanh ghi pipeline giữa các tầng.
  //   Vào: rs1_ex, rs2_ex (thanh ghi lệnh ở EX cần đọc), rd_mem/RegWrite_mem (đích của lệnh ở MEM), rd_wb/RegWrite_wb (đích của lệnh ở WB). Ra: ForwardA, ForwardB (2 bit).
  //   Lưu ý: giá trị lấy từ EX/MEM là kết quả ALU, riêng jal/jalr là PC+4. Phụ thuộc vào lệnh load ngay trước không giải quyết được bằng forwarding -> cần stall (HazardUnit).
  //   a stage can forward only if it writes a register other than x0
  //   Các trường hợp: cả hai tầng cùng ghi thanh ghi mà EX cần -> ưu tiên EX/MEM vì mới hơn. rd = 0 (x0) -> không forward, vì x0 luôn bằng 0. RegWrite = 0 (store, branch) -> không forward.
  //   Forward: 00 register file   01 from MEM/WB   10 from EX/MEM
endmodule

module HazardUnit (
  input  MemRead_ex,
  input  [4:0] rd_ex,
  input  [4:0] rs1_id,
  input  [4:0] rs2_id,
  output stall
);

  wire hit1, hit2, rd_is_x0, rd_ok, uses;

  Comparator #(.mode("unsigned"), .width(5)) comparator_1 (.a(rd_ex), .b({5{1'b0}}), .eq(rd_is_x0));  // open: gt, lt
  Comparator #(.mode("unsigned"), .width(5)) comparator_2 (.a(rd_ex), .b(rs1_id), .eq(hit1));  // open: gt, lt
  Comparator #(.mode("unsigned"), .width(5)) comparator_3 (.a(rd_ex), .b(rs2_id), .eq(hit2));  // open: gt, lt
  not not_1 (rd_ok, rd_is_x0);
  or or_1 (uses, hit1, hit2);
  and and_1 (stall, MemRead_ex, rd_ok, uses);

  // Notes on the sheet:
  //   HazardUnit
  //   Load-use hazard: the instruction in ID needs a value that the load in EX has not read from memory yet -> stall 1 cycle.
  //   ĐƠN VỊ HAZARD (HazardUnit) - phát hiện 'load-use' và yêu cầu dừng pipeline (stall)
  //   stall = (lệnh ở EX là load) VÀ (rd_ex khác x0) VÀ (rd_ex = rs1_id HOẶC rd_ex = rs2_id).
  //   Vấn đề: lệnh load chỉ có dữ liệu ở cuối tầng MEM, nên lệnh liền sau cần nó ở EX sẽ chậm một nhịp; forwarding không cứu được.
  //   Vào: MemRead_ex, rd_ex (lệnh ở EX có phải load và đích là gì), rs1_id, rs2_id (thanh ghi nguồn của lệnh ở ID). Ra: stall = 1 nếu cần dừng.
  //   Các trường hợp: load rồi một lệnh không liên quan rồi mới dùng -> không stall. rd_ex = x0 -> không stall. Chi phí: đúng 1 chu kỳ.
  //   Viết tắt: hazard = rủi ro/xung đột trong pipeline; load-use = lệnh dùng ngay giá trị vừa load; stall = dừng một chu kỳ; bubble = 'bong bóng' (lệnh rỗng NOP chèn vào).
  //   Khi stall = 1: PC và thanh ghi IF/ID giữ nguyên (run = 0), còn từ điều khiển đưa vào ID/EX bị xóa thành 0 (bubble); chu kỳ sau forwarding lấy dữ liệu từ MEM/WB.
  //   rd of the load matches a source of the next instruction
  //   stall = load in EX AND rd != x0 AND (rd == rs1 OR rd == rs2)
endmodule

module Pipeline (
  input  RESET
);

  wire ALUSrc_ex, ALUSrc_id, branch_taken, bubble, CLK, CLK_n, pc_src_ex, run, stall;
  wire [1:0] ALUOp_ex, ALUOp_id, ASel_ex, ASel_id, ForwardA, ForwardB;
  wire [2:0] ctrl_wb, funct3_ex, funct3_id, funct3_mem, ImmSel_id;
  wire [3:0] ALUCtrl;
  wire [4:0] ctrl_mem, rd_ex, rd_id, rd_mem, rd_wb, rs1_ex, rs1_id, rs2_ex, rs2_id;
  wire [6:0] funct7_ex, funct7_id, opcode_id;
  wire [12:0] ctrl_ex, ctrl_id, ctrl_in;
  wire [31:0] alu_a, alu_b, alu_result_ex, alu_result_mem, alu_result_wb, fwd_mem_val, imm_ex, imm_id,
       instr_id, instr_if, instr_in, jalr_target, mem_rdata_mem, mem_rdata_wb, next_pc, opA, opB, pc_ex,
       pc_id, pc_if, pc_plus4_ex, pc_plus4_if, pc_plus4_mem, pc_plus4_wb, pc_target, rs1_data_ex,
       rs1_data_id, rs2_data_ex, rs2_data_id, store_data_mem, target_ex, wb_data;

  Clock clock_1 (.out(CLK));
  not not_1 (CLK_n, CLK);
  Register #(.width(32)) PC (.D(next_pc), .en(run), .clk(CLK), .Q(pc_if), .clr(RESET));
  // Probe on pc_if
  // Probe on pc_id
  // Probe on opA
  Adder #(.width(32)) adder_1 (.a(pc_if), .b(32'h4), .out(pc_plus4_if));  // open: cin, cout
  ROM #(.addrWidth(8), .dataWidth(32)) rom_1 (.addr(pc_if[9:2]), .data(instr_if));
  Multiplexer #(.select(1), .width(32)) multiplexer_1 (
    .in0(pc_plus4_if), .in1(target_ex), .out(next_pc), .sel(pc_src_ex));
  Multiplexer #(.select(1), .width(32)) multiplexer_2 (
    .in0(instr_if), .in1({32{1'b0}}), .out(instr_in), .sel(pc_src_ex));
  not not_2 (run, stall);
  Register #(.width(32)) pc_id_2 (.D(pc_if), .en(run), .clk(CLK), .Q(pc_id));  // open: clr
  Register #(.width(32)) u_instr_id (.D(instr_in), .en(run), .clk(CLK), .Q(instr_id));  // open: clr
  // Probe on instr_id
  // Probe on rs1_data_id
  // Probe on opB
  // Probe on stall
  // Probe on rs2_data_id
  // Probe on alu_a
  InstructionDecode instructiondecode_1 (
    .Instruction(instr_id), .funct7(funct7_id), .rs2(rs2_id), .rs1(rs1_id), .funct3(funct3_id), .rd(rd_id),
    .opcode(opcode_id));
  MainControl maincontrol_1 (
    .opcode(opcode_id), .RegWrite(ctrl_id[0]), .ALUSrc(ALUSrc_id), .MemWrite(ctrl_id[2]),
    .MemRead(ctrl_id[3]), .IsBranch(ctrl_id[4]), .ALUOp(ALUOp_id), .ImmSel(ImmSel_id), .ASel(ASel_id),
    .WBSel(ctrl_id[10:9]), .IsJAL(ctrl_id[11]), .IsJALR(ctrl_id[12]));
  ImmGen immgen_1 (.Instruction(instr_id), .ImmSel(ImmSel_id), .Imm(imm_id));
  RegisterFile registerfile_1 (
    .write_data(wb_data), .CLK(CLK_n), .write(ctrl_wb[0]), .rd(rd_wb), .rs1(rs1_id), .rs2(rs2_id),
    .rs1_data(rs1_data_id), .rs2_data(rs2_data_id));
  HazardUnit hazardunit_1 (.MemRead_ex(ctrl_ex[3]), .rd_ex(rd_ex), .rs1_id(rs1_id), .rs2_id(rs2_id), .stall(stall));
  or or_1 (bubble, stall, pc_src_ex);
  Multiplexer #(.select(1), .width(13)) multiplexer_3 (
    .in0({ctrl_id[12:9], ASel_id, ALUOp_id, ctrl_id[4:2], ALUSrc_id, ctrl_id[0]}), .in1({13{1'b0}}),
    .out(ctrl_in), .sel(bubble));
  // Probe on pc_src_ex
  // Probe on imm_id
  // Probe on alu_b
  Register #(.width(32)) u_pc_ex (.D(pc_id), .en(1'b1), .clk(CLK), .Q(pc_ex));  // open: clr
  Register #(.width(32)) u_rs1_data_ex (.D(rs1_data_id), .en(1'b1), .clk(CLK), .Q(rs1_data_ex));  // open: clr
  Register #(.width(32)) u_rs2_data_ex (.D(rs2_data_id), .en(1'b1), .clk(CLK), .Q(rs2_data_ex));  // open: clr
  Register #(.width(32)) u_imm_ex (.D(imm_id), .en(1'b1), .clk(CLK), .Q(imm_ex));  // open: clr
  Register #(.width(5)) u_rs1_ex (.D(rs1_id), .en(1'b1), .clk(CLK), .Q(rs1_ex));  // open: clr
  Register #(.width(5)) u_rs2_ex (.D(rs2_id), .en(1'b1), .clk(CLK), .Q(rs2_ex));  // open: clr
  Register #(.width(5)) u_rd_ex (.D(rd_id), .en(1'b1), .clk(CLK), .Q(rd_ex));  // open: clr
  Register #(.width(3)) u_funct3_ex (.D(funct3_id), .en(1'b1), .clk(CLK), .Q(funct3_ex));  // open: clr
  Register #(.width(7)) u_funct7_ex (.D(funct7_id), .en(1'b1), .clk(CLK), .Q(funct7_ex));  // open: clr
  Register #(.width(13)) u_ctrl_ex (
    .D(ctrl_in), .en(1'b1), .clk(CLK),
    .Q({ctrl_ex[12:9], ASel_ex, ALUOp_ex, ctrl_ex[4:2], ALUSrc_ex, ctrl_ex[0]}));  // open: clr
  // Probe on ForwardA
  // Probe on pc_ex
  // Probe on target_ex
  Multiplexer #(.select(1), .width(32)) multiplexer_4 (
    .in0(alu_result_mem), .in1(pc_plus4_mem), .out(fwd_mem_val), .sel(ctrl_mem[4]));
  Multiplexer #(.select(2), .width(32)) multiplexer_5 (
    .in0(rs1_data_ex), .in1(wb_data), .in2(fwd_mem_val), .in3(rs1_data_ex), .out(opA), .sel(ForwardA));
  Multiplexer #(.select(2), .width(32)) multiplexer_6 (
    .in0(rs2_data_ex), .in1(wb_data), .in2(fwd_mem_val), .in3(rs2_data_ex), .out(opB), .sel(ForwardB));
  Multiplexer #(.select(2), .width(32)) multiplexer_7 (
    .in0(opA), .in1(pc_ex), .in2({32{1'b0}}), .in3({32{1'b0}}), .out(alu_a), .sel(ASel_ex));
  Multiplexer #(.select(1), .width(32)) multiplexer_8 (.in0(opB), .in1(imm_ex), .out(alu_b), .sel(ALUSrc_ex));
  // Probe on ForwardB
  // Probe on rd_ex
  // Probe on alu_result_mem
  ForwardingUnit forwardingunit_1 (
    .rs1_ex(rs1_ex), .rs2_ex(rs2_ex), .rd_mem(rd_mem), .RegWrite_mem(ctrl_mem[0]), .rd_wb(rd_wb),
    .RegWrite_wb(ctrl_wb[0]), .ForwardA(ForwardA), .ForwardB(ForwardB));
  ALUControl alucontrol_1 (.funct7(funct7_ex), .ALUOp(ALUOp_ex), .funct3(funct3_ex), .ALUCtrl(ALUCtrl));
  ALU alu_1 (.rs1_data(alu_a), .rs2_data(alu_b), .ALU_Ctrl(ALUCtrl), .result(alu_result_ex));
  BranchUnit branchunit_1 (
    .rs1_data(opA), .rs2_data(opB), .IsBranch(ctrl_ex[4]), .funct3(funct3_ex), .branch_taken(branch_taken));
  // Probe on alu_result_ex
  // Probe on ctrl_ex[3]
  // Probe on rd_mem
  Adder #(.width(32)) adder_2 (.a(pc_ex), .b(imm_ex), .out(pc_target));  // open: cin, cout
  assign jalr_target = alu_result_ex & 32'hfffffffe;  // AND_Gate and_1, 32 bits wide
  Multiplexer #(.select(1), .width(32)) multiplexer_9 (
    .in0(pc_target), .in1(jalr_target), .out(target_ex), .sel(ctrl_ex[12]));
  or or_2 (pc_src_ex, branch_taken, ctrl_ex[11], ctrl_ex[12]);
  Adder #(.width(32)) adder_3 (.a(pc_ex), .b(32'h4), .out(pc_plus4_ex));  // open: cin, cout
  Register #(.width(32)) alu_result_mem_2 (.D(alu_result_ex), .en(1'b1), .clk(CLK), .Q(alu_result_mem));  // open: clr
  Register #(.width(32)) u_store_data_mem (.D(opB), .en(1'b1), .clk(CLK), .Q(store_data_mem));  // open: clr
  Register #(.width(32)) u_pc_plus4_mem (.D(pc_plus4_ex), .en(1'b1), .clk(CLK), .Q(pc_plus4_mem));  // open: clr
  Register #(.width(5)) rd_mem_2 (.D(rd_ex), .en(1'b1), .clk(CLK), .Q(rd_mem));  // open: clr
  Register #(.width(3)) u_funct3_mem (.D(funct3_ex), .en(1'b1), .clk(CLK), .Q(funct3_mem));  // open: clr
  Register #(.width(5)) u_ctrl_mem (
    .D({ctrl_ex[10:9], ctrl_ex[3:2], ctrl_ex[0]}), .en(1'b1), .clk(CLK), .Q(ctrl_mem));  // open: clr
  // Probe on wb_data
  // Probe on run
  // Probe on mem_rdata_wb
  // Probe on bubble
  // Probe on rd_wb
  Memory memory_1 (
    .Address(alu_result_mem), .write_data(store_data_mem), .MemWrite(ctrl_mem[1]), .CLK(CLK),
    .funct3(funct3_mem), .read_data(mem_rdata_mem));
  Register #(.width(32)) u_alu_result_wb (.D(alu_result_mem), .en(1'b1), .clk(CLK), .Q(alu_result_wb));  // open: clr
  Register #(.width(32)) mem_rdata_wb_2 (.D(mem_rdata_mem), .en(1'b1), .clk(CLK), .Q(mem_rdata_wb));  // open: clr
  Register #(.width(32)) u_pc_plus4_wb (.D(pc_plus4_mem), .en(1'b1), .clk(CLK), .Q(pc_plus4_wb));  // open: clr
  Register #(.width(5)) rd_wb_2 (.D(rd_mem), .en(1'b1), .clk(CLK), .Q(rd_wb));  // open: clr
  Register #(.width(3)) u_ctrl_wb (.D({ctrl_mem[4:3], ctrl_mem[0]}), .en(1'b1), .clk(CLK), .Q(ctrl_wb));  // open: clr
  // Probe on ctrl_wb[0]
  Multiplexer #(.select(2), .width(32)) multiplexer_10 (
    .in0(alu_result_wb), .in1(mem_rdata_wb), .in2(pc_plus4_wb), .in3({32{1'b0}}), .out(wb_data),
    .sel(ctrl_wb[2:1]));

  // Other names for the same wires on the sheet: ctrl_ex (some bits) = {ASel_ex, ALUOp_ex, ALUSrc_ex};
  //   IsBranch_ex = ctrl_ex[4]; IsJAL_ex = ctrl_ex[11]; IsJALR_ex = ctrl_ex[12]; RegWrite_id = ctrl_id[0];
  //   ctrl_id (some bits) = {ASel_id, ALUOp_id, ALUSrc_id}; MemWrite_id = ctrl_id[2]; MemRead_id = ctrl_id[3];
  //   IsBranch_id = ctrl_id[4]; WBSel_id[1:0] = ctrl_id[10:9]; IsJAL_id = ctrl_id[11]; IsJALR_id = ctrl_id[12];
  //   MemWrite_mem = ctrl_mem[1]; MemRead_mem = ctrl_mem[2];
  //   ctrl_mem_in[4:0] = {ctrl_ex[10:9], ctrl_ex[3:2], ctrl_ex[0]}; RegWrite_ex = ctrl_ex[0];
  //   MemWrite_ex = ctrl_ex[2]; MemRead_ex = ctrl_ex[3]; WBSel_ex[1:0] = ctrl_ex[10:9]; RegWrite_wb = ctrl_wb[0];
  //   WBSel_wb[1:0] = ctrl_wb[2:1]; ctrl_wb_in[2:0] = {ctrl_mem[4:3], ctrl_mem[0]}; RegWrite_mem = ctrl_mem[0];
  //   WBSel_mem[1:0] = ctrl_mem[4:3]; WBSel1_mem = ctrl_mem[4]; pc_word[7:0] = pc_if[9:2]

  // Notes on the sheet:
  //   Clock: Ctrl+F9 = 1 full cycle
  //   RESET = 1 holds PC at 0
  //   CLK_n: the register file writes on the falling edge,
  //   so WB can write and ID can read in the same cycle
  //   CPU PIPELINE 5 TẦNG (Pipeline) - năm lệnh được xử lý cùng lúc, mỗi lệnh ở một tầng
  //   CLK_n = xung nhịp đảo: register file ghi ở cạnh xuống, nên lệnh ở WB ghi và lệnh ở ID đọc trong cùng chu kỳ vẫn thấy giá trị mới.
  //   Vì sao pipeline: chu kỳ xung nhịp có thể ngắn hơn (mỗi tầng chỉ làm một việc); trong Logisim không mô phỏng độ trễ nên số chu kỳ trông không giảm.
  //   PC register (holds while stalled)
  //   BẢNG VIẾT TẮT: IF = Instruction Fetch (nạp lệnh), ID = Instruction Decode (giải mã), EX = Execute (thực thi), MEM = Memory access (truy cập RAM), WB = Write Back (ghi lại).
  //   Xem hiệu quả: bấm Ctrl+F9; các hàng probe ở dưới cho thấy stall, pc_src_ex, ForwardA/B và dữ liệu đi qua từng tầng. Chương trình thử hazard: programs/hazards_demo.hex.
  //   BẢNG THEO DÕI (probe): xem các giá trị này sau mỗi lần bấm Ctrl+F9
  //   PROBE TẦNG ID VÀ EX (vào): lệnh nào đang ở đâu và nó mang theo gì
  //   PROBE TẦNG EX, MEM VÀ WB: dữ liệu đi qua các tầng sau
  //   IF/ID, ID/EX, EX/MEM, MEM/WB = bốn thanh ghi pipeline giữa các tầng, giữ mọi thứ lệnh cần ở tầng sau. Hậu tố _id _ex _mem _wb trong tên dây = tín hiệu của lệnh đang ở tầng đó.
  //   Hazard dữ liệu: lệnh sau cần giá trị lệnh trước chưa ghi xong -> ForwardingUnit lấy từ EX/MEM (Forward = 10) hoặc MEM/WB (01); riêng load rồi dùng ngay -> HazardUnit stall 1 chu kỳ.
  //   Hazard điều khiển: branch/jal/jalr được quyết định ở EX (pc_src_ex = 1) -> PC nhảy tới đích, hai lệnh đã nạp phía sau bị flush thành bubble: mất 2 chu kỳ. Branch không rẽ: không mất gì.
  //   IF - Instruction Fetch
  //   Hazard = xung đột giữa các lệnh đang chạy chồng nhau. Forwarding = chuyển tiếp kết quả về EX. Stall = dừng 1 chu kỳ. Bubble = lệnh rỗng NOP. Flush = hủy các lệnh đã nạp nhầm. CPI = số chu kỳ trên mỗi lệnh.
  //   Từ điều khiển (control word): các tín hiệu điều khiển sinh một lần ở ID, đóng gói rồi đi cùng lệnh qua các thanh ghi pipeline; mỗi tầng tách phần mình cần (13 bit ở ID/EX, 5 bit ở EX/MEM, 3 bit ở MEM/WB).
  //   next PC: PC+4, or the branch / jump target from EX
  //   a taken branch / jump turns the fetched instruction into a bubble (0)
  //   run = not stall: PC and IF/ID only advance when run = 1
  //   PC: địa chỉ đang fetch (đứng yên = stall)
  //   (nhảy khi pc_src_ex = 1)
  //   pc_id: địa chỉ của lệnh
  //   đang ở tầng ID
  //   opA: toán hạng A sau forwarding
  //   (đã chọn theo ForwardA)
  //   PC + 4
  //   contents of rom_1 (hex, n*v repeats v):
  //   00000513 00a00593 00b50533 fff58593 fe059ce3 00a02023 00002603 010000ef 40a606b3 0646a713 0000006f
  //   00c60633 00008067 00000000 00000000 00000000
  //   Instruction ROM 256 x 32
  //   IF/ID registers
  //   instr_id: lệnh đang ở tầng ID
  //   (0 = bubble bị flush)
  //   rs1_data_id: giá trị rs1
  //   đọc ở tầng ID
  //   opB: toán hạng B sau forwarding
  //   (đã chọn theo ForwardB)
  //   InstructionDecode
  //   MainControl
  //   ImmGen
  //   RegisterFile (writes on CLK_n)
  //   HazardUnit: load-use stall
  //   control word (13 bits)
  //   bubble = stall OR flush: the control word becomes 0 (a NOP)
  //   ID - Decode / Register Read
  //   stall = 1: load-use, PC và IF/ID
  //   đứng yên 1 chu kỳ
  //   rs2_data_id: giá trị rs2
  //   đọc ở tầng ID
  //   alu_a: đầu vào A của ALU
  //   (rs1, PC hoặc 0)
  //   pc_src_ex = 1: rẽ nhánh/JAL/JALR,
  //   flush 2 lệnh đã fetch
  //   imm_id: hằng số tức thời
  //   của lệnh ở tầng ID
  //   alu_b: đầu vào B của ALU
  //   (rs2 hoặc imm)
  //   ID/EX registers
  //   RV32I 5-stage pipeline - top level
  //   IF > ID > EX > MEM > WB with pipeline registers between the stages.  Forwarding (EX), load-use stall (ID) and branch / jump flush (EX).
  //   Tunnels with the same name are the same wire.  Suffix _id _ex _mem _wb = the stage a value belongs to.
  //   control word of the instruction in EX
  //   value in EX/MEM that can be forwarded (ALU result, or PC+4 of JAL/JALR)
  //   operand A: 00 register  01 MEM/WB  10 EX/MEM
  //   operand B / store data: same choices
  //   ForwardA: 00 reg, 01 MEM/WB,
  //   10 EX/MEM (toán hạng A)
  //   pc_ex: địa chỉ của lệnh
  //   đang ở tầng EX
  //   target_ex: đích nhảy tính ở EX
  //   (branch/JAL hoặc JALR)
  //   EX - Execute
  //   ALU A: rs1 / PC (auipc) / 0 (lui)
  //   ALU B: rs2 / imm
  //   ForwardingUnit
  //   ForwardB: 00 reg, 01 MEM/WB,
  //   10 EX/MEM (toán hạng B)
  //   rd_ex: số thanh ghi đích
  //   của lệnh ở tầng EX
  //   alu_result_mem: kết quả ALU
  //   của lệnh ở tầng MEM
  //   ALUControl
  //   ALU
  //   BranchUnit
  //   branch / JAL target = PC + imm
  //   JALR target = (rs1 + imm), bit 0 cleared
  //   pc_src_ex = redirect the PC (taken branch, JAL, JALR) and flush IF/ID + ID/EX
  //   link address PC+4
  //   alu_result_ex: kết quả ALU
  //   của lệnh đang ở tầng EX
  //   MemRead_ex = 1: lệnh ở EX là
  //   load (nguồn của stall)
  //   rd_mem: thanh ghi đích
  //   của lệnh ở tầng MEM
  //   pack RegWrite, MemWrite, MemRead, WBSel
  //   EX/MEM registers
  //   wb_data: giá trị ghi vào thanh ghi
  //   ở tầng WB
  //   run = not stall: 0 thì PC
  //   và IF/ID đứng yên
  //   mem_rdata_wb: dữ liệu RAM
  //   của lệnh load ở tầng WB
  //   control word of the instruction in MEM
  //   WBSel bit 1: result is PC+4
  //   MEM - Data Memory
  //   bubble = stall hoặc flush:
  //   từ điều khiển vào ID/EX bị xóa
  //   rd_wb: thanh ghi đích
  //   của lệnh ở tầng WB
  //   Memory
  //   pack RegWrite, WBSel
  //   MEM/WB registers
  //   RegWrite_wb = 1: lệnh ở WB
  //   sẽ ghi thanh ghi
  //   control word of the instruction in WB
  //   WB - Write Back
  //   WBSel: 00 ALU  01 memory  10 PC+4
  //   wb_data goes to the register file (ID) and is also forwarded to EX
endmodule
